// Logisim project 7SegmentIFL.circ as structural Verilog: 2 circuits, main circuit SevenSegment_IFL
module SevenSegment_IFL (
  input  in_1,
  input  [3:0] data,
  input  in_3,
  input  in_4,
  input  in_5,
  input  in_6,
  output a,
  output b,
  output c
);

  wire [6:2] rom_1_data;

  ROM #(.addrWidth(4), .dataWidth(7)) rom_1 (.addr(data), .data({rom_1_data, b, a}));
  _7_Segment_Display u_7_segment_display_1 (.g(in_3), .f(in_1), .a(a), .b(b), .e(in_4), .d(in_5), .c(c), .dp(in_6));

  // Notes on the sheet:
  //   contents of rom_1 (hex, n*v repeats v):
  //   7d
endmodule

module a_segment (
  input  [3:0] data,
  output a
);

  wire and_1_out, and_2_out, and_3_out, not_1_out, not_2_out, not_3_out, not_4_out;

  not not_1 (not_1_out, data[3]);
  and and_1 (and_1_out, not_1_out, not_2_out, not_3_out);
  not not_2 (not_2_out, data[2]);
  not not_3 (not_3_out, data[0]);
  not not_4 (not_4_out, data[2]);
  and and_2 (and_2_out, not_4_out, data[1]);
  and and_3 (and_3_out, data[2], data[0]);
  or or_1 (a, and_1_out, and_2_out, and_3_out, data[3]);
endmodule
