// Logisim project Gray_Counter.circ as structural Verilog: 2 circuits, main circuit main
module main (
  input  Inc,
  output Q1,
  output Q0
);

  wire clk_out, ifl_1_n0, ifl_1_n1;

  Clock clk (.out(clk_out));
  Clock sysclk ();  // open: out
  IFL ifl_1 (.Q1(Q1), .Q0(Q0), .Inc(Inc), .N1(ifl_1_n1), .N0(ifl_1_n0));
  D_Flip_Flop d_ff_1 (.D(ifl_1_n1), .clk(clk_out), .Q(Q1));  // open: Qn, preset, reset
  D_Flip_Flop d_ff_2 (.D(ifl_1_n0), .clk(clk_out), .Q(Q0));  // open: Qn, preset, reset

  // Notes on the sheet:
  //   Joshua Kopaunik
endmodule

module IFL (
  input  Q1,
  input  Q0,
  input  Inc,
  output N1,
  output N0
);

  wire and_1_out, and_2_out, and_3_out, and_4_out, not_1_out, not_2_out, not_3_out;

  not not_1 (not_1_out, Inc);
  not not_2 (not_2_out, Inc);
  not not_3 (not_3_out, Q1);
  and and_1 (and_1_out, Inc, Q0);
  and and_2 (and_2_out, not_1_out, Q1);
  and and_3 (and_3_out, not_2_out, Q0);
  and and_4 (and_4_out, Inc, not_3_out);
  or or_1 (N1, and_1_out, and_2_out);
  or or_2 (N0, and_3_out, and_4_out);

  // Notes on the sheet:
  //   Joshua Kopaunik
  //   This input forming logic only contains AND, OR, and NOT gates
endmodule
