// Logisim project MicroProcessor.circ as structural Verilog: 2 circuits, main circuit main
module main (
  input  Reset,
  output [15:0] out_2
);

  wire Clk_out;
  wire [1:0] InstructionDecoder_data_2, InstructionDecoder_data_3;
  wire [3:0] addrBSegmentDecoder_data, fourbitalu_1_alu_out, multiplexer_1_out, multiplexer_2_out,
       multiplexer_3_out, undriven, undriven_2;
  wire [3:3] eightfile2read_register_1_read_a;
  wire [6:0] addrASegmentDecoder_data, eightfile2read_register_1_read_b, InstructionDecoder_data;
  wire [7:0] ProgramCounter_q;

  Clock Clk (.out(Clk_out));
  TTY tty_1 (.data(eightfile2read_register_1_read_b), .clk(Clk_out), .we(InstructionDecoder_data[1]), .clr(Reset));
  Counter ProgramCounter (
    .clr(Reset), .load(1'b0), .up(1'b1), .count(1'b1), .clk(Clk_out), .Q(ProgramCounter_q));  // open: D, carry
  _7_Segment_Display u_7_segment_display_1 (
    .g(addrASegmentDecoder_data[0]), .f(addrASegmentDecoder_data[1]), .a(addrASegmentDecoder_data[6]),
    .b(addrASegmentDecoder_data[5]), .e(undriven[3]), .d(undriven[2]), .c(undriven[1]), .dp(undriven[0]));
  // Probe on {eightfile2read_register_1_read_a[3], eightfile2read_register_1_read_b}
  _7_Segment_Display u_7_segment_display_2 (
    .g(addrBSegmentDecoder_data[3]), .f(addrBSegmentDecoder_data[2]), .a(addrBSegmentDecoder_data[1]),
    .b(addrBSegmentDecoder_data[0]), .e(undriven_2[3]), .d(undriven_2[2]), .c(undriven_2[1]),
    .dp(undriven_2[0]));
  ROM #(.addrWidth(4), .dataWidth(7)) addrASegmentDecoder (
    .addr(multiplexer_1_out),
    .data({addrASegmentDecoder_data[6:5], undriven[1], undriven[2], undriven[3], addrASegmentDecoder_data[1:0]}));
  Multiplexer #(.width(4), .enable("false")) multiplexer_1 (
    .in0(4'b1111), .in1(eightfile2read_register_1_read_b[3:0]), .out(multiplexer_1_out),
    .sel(InstructionDecoder_data[1]));
  ROM #(.addrWidth(4), .dataWidth(7)) addrBSegmentDecoder (
    .addr(multiplexer_2_out),
    .data({addrBSegmentDecoder_data[1:0], undriven_2[1], undriven_2[2], undriven_2[3], addrBSegmentDecoder_data[2], addrBSegmentDecoder_data[3]}));
  Multiplexer #(.width(4), .enable("false")) multiplexer_2 (
    .in0(4'b1111), .in1({eightfile2read_register_1_read_a[3], eightfile2read_register_1_read_b[6:4]}),
    .out(multiplexer_2_out), .sel(InstructionDecoder_data[1]));
  ROM #(.dataWidth(16)) ProgramROM (.addr(ProgramCounter_q), .data(out_2));
  ROM #(.addrWidth(4), .dataWidth(7)) InstructionDecoder (
    .addr(out_2[15:12]),
    .data({InstructionDecoder_data[6], InstructionDecoder_data_3, InstructionDecoder_data_2, InstructionDecoder_data[1:0]}));
  // Probe on out_2[2:0]
  // Probe on out_2[6:4]
  Multiplexer #(.select(2), .width(4), .enable("false")) multiplexer_3 (
    .in0(out_2[3:0]), .in1(fourbitalu_1_alu_out),
    .in2({eightfile2read_register_1_read_a[3], eightfile2read_register_1_read_b[6:4]}),
    .out(multiplexer_3_out), .sel(InstructionDecoder_data_2));  // open: in3
  // Probe on out_2[10:8]
  // Probe on multiplexer_3_out
  EightFile2Read_Register eightfile2read_register_1 (
    .WE(InstructionDecoder_data[0]), .WAddr(out_2[10:8]), .Data_in(multiplexer_3_out), .Clk(Clk_out),
    .RAddr_A(out_2[6:4]), .RAddr_B(out_2[2:0]),
    .Read_A({eightfile2read_register_1_read_a[3], eightfile2read_register_1_read_b[6:4]}),
    .Read_B(eightfile2read_register_1_read_b[3:0]));
  // Probe on {eightfile2read_register_1_read_a[3], eightfile2read_register_1_read_b[6:4]}
  // Probe on eightfile2read_register_1_read_b[3:0]
  // Probe on InstructionDecoder_data_3
  // Probe on fourbitalu_1_alu_out
  FourBitALU fourbitalu_1 (
    .A({eightfile2read_register_1_read_a[3], eightfile2read_register_1_read_b[6:4]}),
    .B(eightfile2read_register_1_read_b[3:0]), .Subtract(InstructionDecoder_data[6]),
    .S(InstructionDecoder_data_3), .ALU_out(fourbitalu_1_alu_out));

  // Notes on the sheet:
  //   ASCII output
  //   Int outputs
  //   contents of addrASegmentDecoder (hex, n*v repeats v):
  //   7e 30 6d 79 33 5b 5f 70 7f 7b 6*4f
  //   contents of addrBSegmentDecoder (hex, n*v repeats v):
  //   7e 30 6d 79 33 5b 5f 70 7f 7b 6*4f
  //   contents of ProgramROM (hex, n*v repeats v):
  //   1002 1103 3001
  //   contents of InstructionDecoder (hex, n*v repeats v):
  //   0 1 9 2 5 15 25 35 7*0 75
  //   OPCode
  //   Assigns a-g to the correct wires
  //   Assigns a-g to the correct wires
  //   Register Write Addr
  //   Register Read Addr A
  //   Register Read Addr B
  //   Data
  //   AFS ALU Function Select
  //   Subtract
endmodule

module FourBitRegister (
  input  [3:0] Din,
  input  WE,
  input  Clk,
  output [3:0] Dout
);

  wire d_ff_4_q, d_ff_4_qn, multiplexer_1_out, multiplexer_2_out, multiplexer_3_out, multiplexer_4_out,
       undriven, undriven_2, undriven_3;

  Multiplexer #(.enable("false")) multiplexer_1 (.in0(Dout[0]), .in1(Din[0]), .out(multiplexer_1_out), .sel(WE));
  Multiplexer #(.enable("false")) multiplexer_2 (.in0(Dout[1]), .in1(Din[1]), .out(multiplexer_2_out), .sel(WE));
  Multiplexer #(.enable("false")) multiplexer_3 (.in0(Dout[2]), .in1(Din[2]), .out(multiplexer_3_out), .sel(WE));
  Multiplexer #(.enable("false")) multiplexer_4 (.in0(Dout[3]), .in1(Din[3]), .out(multiplexer_4_out), .sel(WE));
  D_Flip_Flop d_ff_1 (.D(multiplexer_1_out), .clk(Clk), .Q(Dout[0]));  // open: Qn, preset, reset
  D_Flip_Flop d_ff_2 (.D(multiplexer_2_out), .clk(Clk), .Q(Dout[1]));  // open: Qn, preset, reset
  D_Flip_Flop d_ff_3 (.D(multiplexer_3_out), .clk(Clk), .Q(Dout[2]));  // open: Qn, preset, reset
  D_Flip_Flop d_ff_4 (
    .clk(undriven), .D(undriven_2), .Q(d_ff_4_q), .Qn(d_ff_4_qn), .preset(multiplexer_4_out),
    .reset(undriven_3));
  D_Flip_Flop d_ff_5 (
    .clk(undriven), .D(undriven_2), .Q(d_ff_4_q), .Qn(d_ff_4_qn), .preset(multiplexer_4_out),
    .reset(undriven_3));

  // Notes on the sheet:
  //   Joshua Kopaunik
endmodule
