// Logisim project Register_File.circ as structural Verilog: 2 circuits, main circuit EightFile2Read_Register
module EightFile2Read_Register (
  input  WE,
  input  [2:0] WAddr,
  input  [3:0] Data_in,
  input  Clk,
  input  [2:0] RAddr_A,
  input  [2:0] RAddr_B,
  output [3:0] Read_A,
  output [3:0] Read_B
);

  wire and_1_out, and_2_out, and_3_out, and_4_out, and_5_out, and_6_out, and_7_out, and_8_out,
       decoder_1_out0, decoder_1_out1, decoder_1_out2, decoder_1_out3, decoder_1_out4, decoder_1_out5,
       decoder_1_out6, decoder_1_out7;
  wire [3:0] four_bit_register_1_dout, four_bit_register_2_dout, four_bit_register_3_dout,
       four_bit_register_4_dout, four_bit_register_5_dout, four_bit_register_6_dout,
       four_bit_register_7_dout, four_bit_register_8_dout;

  Decoder #(.select(3)) decoder_1 (
    .out0(decoder_1_out0), .out1(decoder_1_out1), .out2(decoder_1_out2), .out3(decoder_1_out3),
    .out4(decoder_1_out4), .out5(decoder_1_out5), .out6(decoder_1_out6), .out7(decoder_1_out7), .sel(WAddr),
    .en(WE));
  and and_1 (and_1_out, decoder_1_out0, WE);
  and and_2 (and_2_out, decoder_1_out1, WE);
  and and_3 (and_3_out, decoder_1_out2, WE);
  and and_4 (and_4_out, decoder_1_out3, WE);
  and and_5 (and_5_out, WE, decoder_1_out4);
  and and_6 (and_6_out, WE, decoder_1_out5);
  and and_7 (and_7_out, WE, decoder_1_out6);
  and and_8 (and_8_out, WE, decoder_1_out7);
  Four_bit_register four_bit_register_1 (
    .Din(Data_in), .Write_EN(and_1_out), .Clk(Clk), .Dout(four_bit_register_1_dout));
  Four_bit_register four_bit_register_2 (
    .Din(Data_in), .Write_EN(and_2_out), .Clk(Clk), .Dout(four_bit_register_2_dout));
  Four_bit_register four_bit_register_3 (
    .Din(Data_in), .Write_EN(and_3_out), .Clk(Clk), .Dout(four_bit_register_3_dout));
  Four_bit_register four_bit_register_4 (
    .Din(Data_in), .Write_EN(and_4_out), .Clk(Clk), .Dout(four_bit_register_4_dout));
  Four_bit_register four_bit_register_5 (
    .Din(Data_in), .Write_EN(and_5_out), .Clk(Clk), .Dout(four_bit_register_5_dout));
  Four_bit_register four_bit_register_6 (
    .Din(Data_in), .Write_EN(and_6_out), .Clk(Clk), .Dout(four_bit_register_6_dout));
  Four_bit_register four_bit_register_7 (
    .Din(Data_in), .Write_EN(and_7_out), .Clk(Clk), .Dout(four_bit_register_7_dout));
  Four_bit_register four_bit_register_8 (
    .Din(Data_in), .Write_EN(and_8_out), .Clk(Clk), .Dout(four_bit_register_8_dout));
  Multiplexer #(.select(3), .width(4), .enable("false")) multiplexer_1 (
    .in0(four_bit_register_1_dout), .in1(four_bit_register_2_dout), .in2(four_bit_register_3_dout),
    .in3(four_bit_register_4_dout), .in4(four_bit_register_5_dout), .in5(four_bit_register_6_dout),
    .in6(four_bit_register_7_dout), .in7(four_bit_register_8_dout), .out(Read_A), .sel(RAddr_A));
  Multiplexer #(.select(3), .width(4), .enable("false")) multiplexer_2 (
    .in0(four_bit_register_1_dout), .in1(four_bit_register_2_dout), .in2(four_bit_register_3_dout),
    .in3(four_bit_register_4_dout), .in4(four_bit_register_5_dout), .in5(four_bit_register_6_dout),
    .in6(four_bit_register_7_dout), .in7(four_bit_register_8_dout), .out(Read_B), .sel(RAddr_B));

  // Notes on the sheet:
  //   Joshua Kopaunik
endmodule

module Four_bit_register (
  input  [3:0] Din,
  input  Write_EN,
  input  Clk,
  output [3:0] Dout
);

  wire d_ff_4_q, d_ff_4_qn, multiplexer_1_out, multiplexer_2_out, multiplexer_3_out, multiplexer_4_out,
       undriven, undriven_2, undriven_3;

  Multiplexer #(.enable("false")) multiplexer_1 (.in0(Dout[0]), .in1(Din[0]), .out(multiplexer_1_out), .sel(Write_EN));
  Multiplexer #(.enable("false")) multiplexer_2 (.in0(Dout[1]), .in1(Din[1]), .out(multiplexer_2_out), .sel(Write_EN));
  Multiplexer #(.enable("false")) multiplexer_3 (.in0(Dout[2]), .in1(Din[2]), .out(multiplexer_3_out), .sel(Write_EN));
  Multiplexer #(.enable("false")) multiplexer_4 (.in0(Dout[3]), .in1(Din[3]), .out(multiplexer_4_out), .sel(Write_EN));
  D_Flip_Flop d_ff_1 (.D(multiplexer_1_out), .clk(Clk), .Q(Dout[0]));  // open: Qn, preset, reset
  D_Flip_Flop d_ff_2 (.D(multiplexer_2_out), .clk(Clk), .Q(Dout[1]));  // open: Qn, preset, reset
  D_Flip_Flop d_ff_3 (.D(multiplexer_3_out), .clk(Clk), .Q(Dout[2]));  // open: Qn, preset, reset
  D_Flip_Flop d_ff_4 (
    .clk(undriven), .D(undriven_2), .Q(d_ff_4_q), .Qn(d_ff_4_qn), .preset(multiplexer_4_out),
    .reset(undriven_3));
  D_Flip_Flop d_ff_5 (
    .clk(undriven), .D(undriven_2), .Q(d_ff_4_q), .Qn(d_ff_4_qn), .preset(multiplexer_4_out),
    .reset(undriven_3));

  // Notes on the sheet:
  //   Joshua Kopaunik
endmodule
