// Logisim project Ring_Counter.circ as structural Verilog: 1 circuit, main circuit main
module main (
  input  Reset,
  output Q2,
  output Q1,
  output Q0
);

  wire clk_out;

  Clock clk (.out(clk_out));
  Clock sysclk ();  // open: out
  D_Flip_Flop d_ff_1 (.D(Q1), .clk(clk_out), .Q(Q2), .reset(Reset));  // open: Qn, preset
  D_Flip_Flop d_ff_2 (.D(Q0), .clk(clk_out), .Q(Q1), .reset(Reset));  // open: Qn, preset
  D_Flip_Flop d_ff_3 (.D(Q2), .clk(clk_out), .Q(Q0), .preset(Reset));  // open: Qn, reset

  // Notes on the sheet:
  //   Joshua Kopaunik
endmodule
